# Fritzing sketch sketch (saved by Fritzing 0.9.3b)
stripboards: 1

parts:
  IC1 = ULN2803A [package=THT]
  U3 = mystery part, 28 pins [chip_label="Wi Py 2.0"]
  U4 = Voltage Regulator [package=to220-igo]
  C2 = Ceramic Capacitor [capacitance=100nF voltage=20V package="100 mil [THT, multilayer]"]
  C3 = Ceramic Capacitor [capacitance=100nF voltage=20V package="100 mil [THT, multilayer]"]
  C4 = Electrolytic Capacitor [capacitance=10µF package="100 mil [THT, electrolytic]"]
  J1 = double row male pin header, 2 pins [form="♂ (male)"]
  D1 = Rectifier Diode [part_number=1N4001 package="300 mil [THT]"]
  J2 = double row male pin header, 8 pins [form="♂ (male)"]
  IC2 = ULN2803A [package=THT]
  J3 = double row male pin header, 8 pins [form="♂ (male)"]
  J4 = double row male pin header, 12 pins [form="♂ (male)"]
  J5 = double row male pin header, 2 pins [form="♂ (male)"]

nets:
  N1: IC1.In_1, U3.pin12
  N2: IC1.In_2, U3.pin11
  N3: IC1.In_3, U3.pin10
  N4: IC1.In_4, U3.pin9
  N5: IC1.In_5, U3.pin8
  N6: IC1.In_6, U3.pin7
  N7: IC1.In_7, U3.pin6
  N8: IC1.In_8, U3.pin5
  N9: IC1.0V, U3.pin27, U4.GND, C3.0, C4.-, J1.pin2
  N10: IC1.Out_8, J2.pin1
  N11: IC1.Out_7, J2.pin2
  N12: IC1.Out_6, J2.pin3
  N13: IC1.Out_5, J2.pin4
  N14: IC1.Out_4, J2.pin5
  N15: IC1.Out_3, J2.pin6
  N16: IC1.Out_2, J2.pin7
  N17: IC1.Out_1, J2.pin8
  N18: U3.pin2, J5.pin1
  N19: U3.pin3, J5.pin2
  N20: U3.pin13, IC2.0V
  N21: U3.pin14, IC2.In_8
  N22: U3.pin21, IC2.In_3
  N23: U3.pin22, IC2.In_4
  N24: U3.pin23, IC2.In_5
  N25: U3.pin24, IC2.In_6
  N26: U3.pin25, IC2.In_7
  N27: U3.pin28, U4.OUT, C2.1, J4.pin1, J4.pin2, J4.pin3, J4.pin4, J4.pin5, J4.pin6, J4.pin7, J4.pin8, J4.pin9, J4.pin10, J4.pin11, J4.pin12
  N28: U4.IN, C2.0, C3.1, C4.+, D1.cathode
  N29: J1.pin1, D1.anode
  N30: IC2.In_1, IC2.Out_1
  N31: IC2.COM_-_Common, J3.pin1
  N32: IC2.Out_8, J3.pin2
  N33: IC2.Out_7, J3.pin3
  N34: IC2.Out_6, J3.pin4
  N35: IC2.Out_5, J3.pin5
  N36: IC2.Out_4, J3.pin6
  N37: IC2.Out_3, J3.pin7
  N38: IC2.Out_2, J3.pin8
